# Fritzing sketch schematic (saved by Fritzing 0.9.3b)
breadboards: 1

parts:
  U1 = attiny85 [package=dip]
  Part1 = Arduino Uno (Rev3)
  C1 = Ceramic Capacitor [capacitance=100nF package="100 mil [THT, multilayer]"]
  R1 = Resistor [tolerance=±5% resistance=330 package=THT]
  LED1 = LED - 5mm [color="Red (633nm)" package="5 mm [THT]"]
  C2 = Electrolytic Capacitor [capacitance=0.1µF package="100 mil [THT, electrolytic]"]

nets:
  N1: U1.Pin_1, Part1.D10_PWM/SS
  N2: U1.Pin_4, Part1.GND, C1.0, LED1.cathode, C2.-
  N3: U1.Pin_5, Part1.D11_PWM/MOSI
  N4: U1.Pin_6, Part1.D12/MISO, R1.Pin_1
  N5: U1.Pin_7, Part1.D13/SCK
  N6: U1.Pin_8, Part1.5V, C1.1
  N7: Part1.RESET, C2.+
  N8: R1.Pin_0, LED1.anode

notes:
  100nF
  10uF
